# Fritzing sketch Breadboard Design (saved by Fritzing 0.8.3b)
breadboards: 1
perfboards: 6

parts:
  U1 = atmega328 [package=dip]
  U2 = LIPO-1000mAh [package=lipo-1000]
  R1 = Resistor [tolerance=±5% resistance=10k package=THT]
  Y1 = Resonator [frequency="16 Mhz" package=THT]
  C2 = Electrolytic Capacitor [capacitance=10µF package="0807 [SMD, electrolytic]"]
  J1 = female pin header, 10 pins [form="♀ (female)"]  # not connected
  J2 = female pin header, 4 pins [form="♀ (female)"]  # not connected
  M1 = DC Motor
  M2 = DC Motor
  M3 = DC Motor
  M4 = DC Motor
  Q1 = NPN-Transistor [package="TO92 [THT]"]
  J3 = female pin header, 4 pins [form="♀ (female)"]
  J4 = female pin header, 4 pins [form="♀ (female)"]
  R2 = Resistor [tolerance=±5% resistance=10k package=THT]
  R3 = Resistor [tolerance=±5% resistance=10k package=THT]
  Q2 = NPN-Transistor [package="TO92 [THT]"]
  R4 = Resistor [tolerance=±5% resistance=10k package=THT]
  Q3 = NPN-Transistor [package="TO92 [THT]"]
  R5 = Resistor [tolerance=±5% resistance=10k package=THT]
  Q4 = NPN-Transistor [package="TO92 [THT]"]
  Part1 = Arduino Uno (Rev3)
  J5 = female pin header, 4 pins [form="♀ (female)"]
  J6 = female pin header, 4 pins [form="♀ (female)"]

nets:
  N1: U1.RESET, R1.Pin_1
  N2: U1.D3_(PWM), R4.Pin_0
  N3: U1.VCC, U1.AVCC, U1.AREF, U2.+, C2.+, M1.pin_1, M2.pin_1, M3.pin_1, M4.pin_1, J3.pin4
  GND: U1.GND, U2.-, R1.Pin_0, Y1.GND, C2.-, Q1.C, J4.pin4, Q2.C, Q3.C, Q4.C
  N4: U1.XLAT1, Y1.0
  N5: U1.XLAT2, Y1.pin_1
  N6: U1.D6_(PWM), R3.Pin_0
  N7: U1.D9_(PWM), R2.Pin_0
  N8: U1.D10_(PWM), R5.Pin_0
  N9: U1.D11_(PWM), J3.pin2
  N10: U1.D12, J4.pin1
  N11: U1.D13, J4.pin2
  N12: U1.A1, J4.pin3
  N13: U1.A2, J3.pin3
  N14: M1.pin_2, Q2.E
  N15: M2.pin_2, Q1.E
  N16: M3.pin_2, Q3.E
  N17: M4.pin_2, Q4.E
  N18: Q1.B, R5.Pin_1
  N19: R2.Pin_1, Q3.B
  N20: R3.Pin_1, Q4.B
  N21: Q2.B, R4.Pin_1
  N22: Part1.ICSP_MISO, Part1.D12/MISO, J5.pin1
  N23: Part1.ICSP_SCK, Part1.D13/SCK, J5.pin2
  N24: Part1.ICSP_MOSI, Part1.D11_PWM/MOSI, J6.pin2
  N25: Part1.GND, J5.pin4
  N26: Part1.D9_PWM, J5.pin3
  N27: Part1.D10_PWM/SS, J6.pin3
  N28: Part1.5V, J6.pin4
