# Fritzing sketch Beam Me Up (PCB) (saved by Fritzing 0.8.3b)
circuit board: 5.33115cm x 4.31518cm

parts:
  R3 = Resistor [tolerance=±5% resistance=10k package=THT]
  ATMEGA = atmega328 [package=dip]
  M1 = DC Motor
  R5 = Resistor [tolerance=±5% resistance=10k package=THT]
  M4 = DC Motor
  Y1 = Resonator [frequency="16 Mhz" package=THT]
  R2 = Resistor [tolerance=±5% resistance=10k package=THT]
  M2 = DC Motor
  R4 = Resistor [tolerance=±5% resistance=10k package=THT]
  Q1 = NPN-Transistor [package="TO92 [THT]"]
  Q4 = NPN-Transistor [package="TO92 [THT]"]
  R1 = Resistor [tolerance=±5% resistance=10k package=THT]
  C1 = Electrolytic Capacitor [capacitance=10µF package="100 mil [THT, electrolytic]"]
  M3 = DC Motor
  Q2 = NPN-Transistor [package="TO92 [THT]"]
  J1 = female pin header, 2 pins [form="♀ (female)"]
  3_7V = Battery
  R6 = Resistor [tolerance=±5% resistance=10k package=THT]
  L1 = LED - 3mm [color="Red (633nm)" package="3 mm [THT]"]
  C2 = Capacitor [package=cap-pth-small2]
  C3 = Capacitor [package=cap-pth-small2]
  Q3 = NPN-Transistor [package="TO92 [THT]"]

nets:
  N1: R3.Pin_0, ATMEGA.D9_(PWM)
  N2: R3.Pin_1, Q3.B
  N3: ATMEGA.RESET, R5.Pin_1
  N4: ATMEGA.D2, L1.anode
  N5: ATMEGA.D3_(PWM), R1.Pin_1
  N6: ATMEGA.VCC, M1.pin_2, R5.Pin_0, M2.pin_2, J1.pin1
  GND: ATMEGA.GND, Y1.GND, Q1.E, Q4.E, C1.-, Q2.E, 3_7V.-, R6.Pin_0, C2.1, C3.1, Q3.E
  N7: ATMEGA.XLAT1, Y1.0, C2.2
  N8: ATMEGA.XLAT2, Y1.pin_1, C3.2
  N9: ATMEGA.D6_(PWM), R4.Pin_1
  N10: ATMEGA.D10_(PWM), R2.Pin_0
  N11: ATMEGA.AVCC, ATMEGA.AREF, M4.pin_2, M3.pin_2, J1.pin2
  N12: M1.pin_1, Q1.C
  N13: M4.pin_1, Q4.C
  N14: R2.Pin_1, Q2.B
  N15: M2.pin_1, Q2.C
  N16: R4.Pin_0, Q4.B
  N17: Q1.B, R1.Pin_0
  N18: C1.+, 3_7V.+
  N19: M3.pin_1, Q3.C
  N20: R6.Pin_1, L1.cathode

notes:
  +
  -
