# Fritzing sketch Beam Me Up (Schematic) (saved by Fritzing 0.8.3b)

parts:
  U1 = atmega328 [package=dip]
  R5 = Resistor [tolerance=±5% resistance=10k package=THT]  # not connected
  Y1 = Resonator [frequency="16 Mhz" package=THT]
  Q1 = NPN-Transistor [package="TO92 [THT]"]
  R1 = Resistor [tolerance=±5% resistance=10k package=THT]  # not connected
  M1 = DC Motor  # not connected
  M2 = DC Motor  # not connected
  Q2 = NPN-Transistor [package="TO92 [THT]"]
  R2 = Resistor [tolerance=±5% resistance=10k package=THT]  # not connected
  M3 = DC Motor  # not connected
  Q3 = NPN-Transistor [package="TO92 [THT]"]
  R3 = Resistor [tolerance=±5% resistance=10k package=THT]  # not connected
  M4 = DC Motor  # not connected
  Q4 = NPN-Transistor [package="TO92 [THT]"]
  R4 = Resistor [tolerance=±5% resistance=10k package=THT]  # not connected
  C1 = Electrolytic Capacitor [capacitance=10µF package="100 mil [THT, electrolytic]"]

nets:
  3.7V: U1.VCC, U1.AVCC, U1.AREF, C1.+
  GND: U1.GND, Q1.E, Q2.E, Q3.E, C1.-
  N1: U1.XLAT1, Y1.0
  N2: U1.XLAT2, Y1.pin_1
  N3: Y1.GND, Q4.E
